// Logisim project cpu.circ as structural Verilog
module main (
);

  wire dipswitch_1_sw1;
  wire [2:0] dipswitch_1_sw4;

  memoryCell Addressing (.Din(dipswitch_1_sw1));  // open: WE, CLK, OE, RESET, Dout, StoredData
  DipSwitch #(.number(16)) dipswitch_1 (
    .sw1(dipswitch_1_sw1), .sw2(dipswitch_1_sw4[2]), .sw3(dipswitch_1_sw4[1]), .sw4(dipswitch_1_sw4[0]));  // open: sw5, sw6, sw7, sw8, sw9, sw10, sw11, sw12, sw13, sw14, sw15, sw16
  Decoder #(.enable("false"), .select(3)) decoder_1 (.sel(dipswitch_1_sw4));  // open: out0, out1, out2, out3, out4, out5, out6, out7
  Functional_Register PC ();  // open: INC, LD, CLR, CLK, Din, Dout
  Functional_Register DR ();  // open: INC, LD, CLR, CLK, Din, Dout
  Functional_Register AC ();  // open: INC, LD, CLR, CLK, Din, Dout
  Functional_Register IR ();  // open: INC, LD, CLR, CLK, Din, Dout
  Functional_Register TR ();  // open: INC, LD, CLR, CLK, Din, Dout
endmodule

module memoryCell (
  input  WE,
  input  Din,
  input  CLK,
  input  OE,
  input  RESET,
  output Dout,
  output StoredData
);

  wire and_1_out, and_2_out, not_1_out, or_1_out;

  not not_1 (not_1_out, WE);
  and and_1 (and_1_out, StoredData, not_1_out);
  and and_2 (and_2_out, WE, Din);
  or or_1 (or_1_out, and_1_out, and_2_out);
  D_Flip_Flop d_ff_1 (.D(or_1_out), .clk(CLK), .Q(StoredData), .reset(RESET));  // open: Qn, preset
  assign Dout = OE ? StoredData : 1'bz;  // Controlled_Buffer controlled_buffer_1
endmodule

module Register_16bit (
  input  CLK,
  input  WE,
  input  OE,
  input  Reset,
  input  [15:0] Din,
  output [15:0] Dout,
  output [15:0] StoredData
);

  memoryCell memorycell_1 (
    .WE(WE), .Din(Din[0]), .CLK(CLK), .OE(OE), .RESET(Reset), .Dout(Dout[0]), .StoredData(StoredData[0]));
  memoryCell memorycell_2 (
    .WE(WE), .Din(Din[1]), .CLK(CLK), .OE(OE), .RESET(Reset), .Dout(Dout[1]), .StoredData(StoredData[1]));
  memoryCell memorycell_3 (
    .WE(WE), .Din(Din[2]), .CLK(CLK), .OE(OE), .RESET(Reset), .Dout(Dout[2]), .StoredData(StoredData[2]));
  memoryCell memorycell_4 (
    .WE(WE), .Din(Din[3]), .CLK(CLK), .OE(OE), .RESET(Reset), .Dout(Dout[3]), .StoredData(StoredData[3]));
  memoryCell memorycell_5 (
    .WE(WE), .Din(Din[4]), .CLK(CLK), .OE(OE), .RESET(Reset), .Dout(Dout[4]), .StoredData(StoredData[4]));
  memoryCell memorycell_6 (
    .WE(WE), .Din(Din[5]), .CLK(CLK), .OE(OE), .RESET(Reset), .Dout(Dout[5]), .StoredData(StoredData[5]));
  memoryCell memorycell_7 (
    .WE(WE), .Din(Din[6]), .CLK(CLK), .OE(OE), .RESET(Reset), .Dout(Dout[6]), .StoredData(StoredData[6]));
  memoryCell memorycell_8 (
    .WE(WE), .Din(Din[7]), .CLK(CLK), .OE(OE), .RESET(Reset), .Dout(Dout[7]), .StoredData(StoredData[7]));
  memoryCell memorycell_9 (
    .WE(WE), .Din(Din[8]), .CLK(CLK), .OE(OE), .RESET(Reset), .Dout(Dout[8]), .StoredData(StoredData[8]));
  memoryCell memorycell_10 (
    .WE(WE), .Din(Din[9]), .CLK(CLK), .OE(OE), .RESET(Reset), .Dout(Dout[9]), .StoredData(StoredData[9]));
  memoryCell memorycell_11 (
    .WE(WE), .Din(Din[10]), .CLK(CLK), .OE(OE), .RESET(Reset), .Dout(Dout[10]), .StoredData(StoredData[10]));
  memoryCell memorycell_12 (
    .WE(WE), .Din(Din[11]), .CLK(CLK), .OE(OE), .RESET(Reset), .Dout(Dout[11]), .StoredData(StoredData[11]));
  memoryCell memorycell_13 (
    .WE(WE), .Din(Din[12]), .CLK(CLK), .OE(OE), .RESET(Reset), .Dout(Dout[12]), .StoredData(StoredData[12]));
  memoryCell memorycell_14 (
    .WE(WE), .Din(Din[13]), .CLK(CLK), .OE(OE), .RESET(Reset), .Dout(Dout[13]), .StoredData(StoredData[13]));
  memoryCell memorycell_15 (
    .WE(WE), .Din(Din[14]), .CLK(CLK), .OE(OE), .RESET(Reset), .Dout(Dout[14]), .StoredData(StoredData[14]));
  memoryCell memorycell_16 (
    .WE(WE), .Din(Din[15]), .CLK(CLK), .OE(OE), .RESET(Reset), .Dout(Dout[15]), .StoredData(StoredData[15]));
endmodule

module Register_11bit (
  input  CLK,
  input  WE,
  input  OE,
  input  Reset,
  input  [11:0] in_5,
  output [11:0] Dout,
  output [11:0] StoredData
);

  memoryCell memorycell_1 (
    .WE(WE), .Din(in_5[0]), .CLK(CLK), .OE(OE), .RESET(Reset), .Dout(Dout[0]), .StoredData(StoredData[0]));
  memoryCell memorycell_2 (
    .WE(WE), .Din(in_5[1]), .CLK(CLK), .OE(OE), .RESET(Reset), .Dout(Dout[1]), .StoredData(StoredData[1]));
  memoryCell memorycell_3 (
    .WE(WE), .Din(in_5[2]), .CLK(CLK), .OE(OE), .RESET(Reset), .Dout(Dout[2]), .StoredData(StoredData[2]));
  memoryCell memorycell_4 (
    .WE(WE), .Din(in_5[3]), .CLK(CLK), .OE(OE), .RESET(Reset), .Dout(Dout[3]), .StoredData(StoredData[3]));
  memoryCell memorycell_5 (
    .WE(WE), .Din(in_5[4]), .CLK(CLK), .OE(OE), .RESET(Reset), .Dout(Dout[4]), .StoredData(StoredData[4]));
  memoryCell memorycell_6 (
    .WE(WE), .Din(in_5[5]), .CLK(CLK), .OE(OE), .RESET(Reset), .Dout(Dout[5]), .StoredData(StoredData[5]));
  memoryCell memorycell_7 (
    .WE(WE), .Din(in_5[6]), .CLK(CLK), .OE(OE), .RESET(Reset), .Dout(Dout[6]), .StoredData(StoredData[6]));
  memoryCell memorycell_8 (
    .WE(WE), .Din(in_5[7]), .CLK(CLK), .OE(OE), .RESET(Reset), .Dout(Dout[7]), .StoredData(StoredData[7]));
  memoryCell memorycell_9 (
    .WE(WE), .Din(in_5[8]), .CLK(CLK), .OE(OE), .RESET(Reset), .Dout(Dout[8]), .StoredData(StoredData[8]));
  memoryCell memorycell_10 (
    .WE(WE), .Din(in_5[9]), .CLK(CLK), .OE(OE), .RESET(Reset), .Dout(Dout[9]), .StoredData(StoredData[9]));
  memoryCell memorycell_11 (
    .WE(WE), .Din(in_5[10]), .CLK(CLK), .OE(OE), .RESET(Reset), .Dout(Dout[10]), .StoredData(StoredData[10]));
  memoryCell memorycell_12 (
    .WE(WE), .Din(in_5[11]), .CLK(CLK), .OE(OE), .RESET(Reset), .Dout(Dout[11]), .StoredData(StoredData[11]));
endmodule

module CU (
  input  I,
  input  [7:0] Decoder_Input_8,
  input  [11:0] IR_0_to_11,
  input  [15:0] TimingControl
);
endmodule

module Increment_16bit (
  input  [15:0] InputData,
  output [15:0] StoredData
);

  Adder #(.width(16)) adder_1 (.a(InputData), .b(16'h1), .out(StoredData));  // open: cin, cout
endmodule

module Functional_Register (
  input  INC,
  input  LD,
  input  CLR,
  input  CLK,
  input  [15:0] Din,
  output [15:0] Dout
);

  wire [15:0] increment_16bit_1_storeddata, multiplexer_1_out, multiplexer_2_out, multiplexer_3_out;

  Multiplexer #(.width(16)) multiplexer_1 (
    .in1(increment_16bit_1_storeddata), .out(multiplexer_1_out), .sel(INC));  // open: in0
  Multiplexer #(.width(16)) multiplexer_2 (.in0(multiplexer_1_out), .in1(Din), .out(multiplexer_2_out), .sel(LD));
  Multiplexer #(.width(16)) multiplexer_3 (
    .in0(multiplexer_2_out), .in1({16{1'b0}}), .out(multiplexer_3_out), .sel(CLR));
  Increment_16bit increment_16bit_1 (.InputData(Dout), .StoredData(increment_16bit_1_storeddata));
  Register_16bit register_16bit_1 (
    .CLK(CLK), .WE(1'b1), .OE(1'b1), .Din(multiplexer_3_out), .Dout(Dout));  // open: Reset, StoredData
endmodule
