// Logisim project cpu.circ as structural Verilog
module memoryCell (
  input  WE,
  input  Din,
  input  CLK,
  input  OE,
  input  in_5,
  output Dout,
  output StoredData
);

  wire and_1_out, and_2_out, not_1_out, or_1_out;

  not not_1 (not_1_out, WE);
  and and_1 (and_1_out, StoredData, not_1_out);
  and and_2 (and_2_out, WE, Din);
  or or_1 (or_1_out, and_1_out, and_2_out);
  D_Flip_Flop d_ff_1 (.D(or_1_out), .clk(CLK), .Q(StoredData), .reset(in_5));  // open: Qn, preset
  assign Dout = OE ? StoredData : 1'bz;  // Controlled_Buffer controlled_buffer_1
endmodule
